# Fritzing sketch arduino sheme (saved by Fritzing 0.8.7b)
perfboards: 1

parts:
  Part1 = Arduino Uno (Rev3)
  IR1 = TSOP312.., 314.. [package=THT]
  12V_power = Power plug
  Q1 = Basic FET P-Channel [package="TO220 [THT]"]
  Q2 = Basic FET P-Channel [package="TO220 [THT]"]
  Q3 = Basic FET P-Channel [package="TO220 [THT]"]
  R1 = Resistor [package="2010 [SMD]"]
  R2 = Resistor [package="2010 [SMD]"]
  LED_STRIP = RGB LED (com. anode, rbg) [package="5 mm [THT]"]
  R3 = Resistor [package="2010 [SMD]"]

nets:
  N1: Part1.D10_PWM/SS, R2.Pin_0
  N2: Part1.D11_PWM/MOSI, R3.Pin_0
  GND: Part1.GND, IR1.GND, 12V_power.GND, Q1.source, Q2.source, Q3.source
  N3: Part1.D5_PWM, R1.Pin_0
  N4: Part1.D7, IR1.Data
  N5: Part1.5V, IR1.Vs
  N6: 12V_power.VCC, LED_STRIP.common_anode
  N7: Q1.gate, R3.Pin_1
  N8: Q1.drain, LED_STRIP.green_cathode
  N9: Q2.gate, R2.Pin_1
  N10: Q2.drain, LED_STRIP.blue_cathode
  N11: Q3.gate, R1.Pin_1
  N12: Q3.drain, LED_STRIP.red_cathode
